# Fritzing sketch sound coin bank (saved by Fritzing 0.8.7b)
breadboards: 1

parts:
  부품1 = Arduino Uno (Rev3) - ICSP
  R1 = Resistor [tolerance=±5% resistance=10k package=THT]

nets:
  N1: 부품1.GND, R1.Pin_1
  N2: 부품1.D2, R1.Pin_0
